# Fritzing sketch dakoku-board (saved by Fritzing 0.9.3b)
breadboards: 1

parts:
  W1 = ESP-WROOM2-02 full breakout [package="DIP (Dual Inline) [THT]"]
  パーツ1 = LCD1602-I2C
  U2 = SCREENKEYMATINGCONNECTOR [package=screenkeymatingconnector]

nets:
  3V3: W1.3V3, パーツ1.VCC, U2.14
  N1: W1.IO14, U2.13
  N2: W1.IO12, U2.12
  N3: W1.IO4, パーツ1.SDA
  N4: W1.IO5, パーツ1.SCL
  GND: W1.GND, パーツ1.GND, U2.9, U2.11

notes:
  SONYのFeliCaリーダー

custom parts:
  LCD1602-I2C: A standard character display, usually with 2x16 characters. Comes in many colors with LCM1602 IIC attached.
